# Fritzing sketch SmartWater (saved by Fritzing 0.9.4)
breadboards: 1

parts:
  ESP32 = ESP32-38PinWide [part_number=ESP32-38PinWide]
  元件1 = SRF05 Ultrasonic Rangefinder
  OLED1 = OLED 128x64 I2C Monochrome Display
  DS1 = DS18B20 1-Wire Temperature Sensor [part_number=DS18B20]
  R1 = Resistor [tolerance=±5% resistance=4.7k package="0805 [SMD]"]
  RELAY = KY-019 5V Relay Module [package="Breakout board"]
  RELAY_2 = KY-019 5V Relay Module [package="Breakout board"]
  WATER_VALVE = Plastic Solenoid Valve
  YF-S201_Flow_Meter1 = YF-S201 Water Flow Meter
  WATER_PUMP = water pump/motor
  ACV = AC Power [voltage=110V frequency=60]

nets:
  N1: ESP32.3.3, OLED1.VDD
  N2: ESP32.GPIO27, DS1.DQ, R1.Pin_0
  N3: ESP32.GPIO14, YF-S201_Flow_Meter1.SIG
  N4: ESP32.GPIO12, 元件1.Trig
  GND: ESP32.GND, 元件1.GND, OLED1.GND, DS1.GND, RELAY.-, RELAY_2.-, YF-S201_Flow_Meter1.GND
  N5: ESP32.GPIO13, 元件1.Echo
  VCC: ESP32.VIN, 元件1.VCC, DS1.VDD, R1.Pin_1, RELAY.+, RELAY_2.+, YF-S201_Flow_Meter1.VCC
  N6: ESP32.GPIO21, OLED1.SDA
  N7: ESP32.GPIO22, OLED1.SCK
  N8: RELAY.Common, RELAY_2.Common, ACV.V-
  N9: RELAY.NO, WATER_PUMP.pin_2
  N10: RELAY_2.NO, WATER_VALVE.no_name_yet#2
  N11: WATER_VALVE.no_name_yet#1, WATER_PUMP.pin_1, ACV.V+

notes:
  ACV GND
  ACV 110V

custom parts:
  ESP32-38PinWide: Generic 38-Pin ESP32 with wide format (only access to one side of pins on a breadboard) based on Stephen Lilley's HiLetgo ESP-WROOM-32 ESP32 ESP-32S Development Board.
  KY-019 5V Relay Module: KY-019 5V Relay module, used to control AC circuits. (Special thanks to vanepp for fixing the PCB holes and other errors)
  YF-S201 Water Flow Meter: The YF-S201 Flow Meter. The input voltage is 5V to 24V (DC).
  water pump/motor: WATER PUMP BY ARDUBLOCKTR
